// Logisim project Laboratorio2.circ as structural Verilog: 4 circuits, main circuit main
module main (
  input  in_1,
  input  in_2
);

  wire button_1_out, button_2_out, button_3_out, button_4_out;
  wire [6:0] D, Dp, U, Up;

  Button button_1 (.out(button_1_out));
  Button button_2 (.out(button_2_out));
  Joystick joystick_1 ();  // open: x, y
  // DotMatrix #(.dotshape("circle"), .inputtype("select"), .matrixcols(16), .matrixrows(17)) dotmatrix_1: pin names not known
  ContadorUnitario contadorunitario_1 (
    .action(in_1), .push(button_1_out), .Reset(button_2_out), .Decenas(D), .Unidades(U));
  _7_Segment_Display #(.decimalPoint("false")) u_7_segment_display_1 (
    .g(D[6]), .f(D[5]), .a(D[0]), .b(D[1]), .e(D[4]), .d(D[3]), .c(D[2]));
  _7_Segment_Display #(.decimalPoint("false")) u_7_segment_display_2 (
    .g(Dp[6]), .f(Dp[5]), .a(Dp[0]), .b(Dp[1]), .e(Dp[4]), .d(Dp[3]), .c(Dp[2]));
  Button button_3 (.out(button_3_out));
  Button button_4 (.out(button_4_out));
  _7_Segment_Display #(.decimalPoint("false")) u_7_segment_display_3 (
    .g(U[6]), .f(U[5]), .a(U[0]), .b(U[1]), .e(U[4]), .d(U[3]), .c(U[2]));
  _7_Segment_Display #(.decimalPoint("false")) u_7_segment_display_4 (
    .g(Up[6]), .f(Up[5]), .a(Up[0]), .b(Up[1]), .e(Up[4]), .d(Up[3]), .c(Up[2]));
  ContadorUnitario contadorunitario_2 (
    .action(in_2), .push(button_3_out), .Reset(button_4_out), .Decenas(Dp), .Unidades(Up));

  // Notes on the sheet:
  //   "Catch a falling star"
  //   Estrellas Atrapadas
  //   Estrellas Pasadas
endmodule

module BCD7SEG (
  input  min,
  input  in_2,
  input  in_3,
  input  max,
  output a,
  output b,
  output c,
  output d,
  output e,
  output f,
  output g
);

  wire and_1_out, and_2_out, and_3_out, and_4_out, and_5_out, and_6_out, and_7_out, and_8_out, and_9_out,
       and_10_out, and_11_out, and_12_out, and_13_out, and_14_out, and_15_out, and_16_out, and_17_out,
       and_18_out, and_19_out, and_20_out, and_21_out, and_22_out, and_23_out, and_24_out, and_25_out,
       not_1_out, not_2_out, not_3_out, not_4_out;

  not not_1 (not_1_out, max);
  not not_2 (not_2_out, in_3);
  not not_3 (not_3_out, in_2);
  not not_4 (not_4_out, min);
  and and_1 (and_1_out, not_1_out, not_2_out, not_4_out);
  and and_2 (and_2_out, not_1_out, in_2);
  and and_3 (and_3_out, not_1_out, in_3, min);
  and and_4 (and_4_out, max, not_2_out, not_3_out);
  and and_5 (and_5_out, not_1_out, not_2_out);
  and and_6 (and_6_out, not_1_out, not_3_out, not_4_out);
  and and_7 (and_7_out, not_2_out, not_3_out);
  and and_8 (and_8_out, not_1_out, in_2, min);
  and and_9 (and_9_out, not_2_out, not_3_out);
  and and_10 (and_10_out, not_1_out, min);
  and and_11 (and_11_out, not_1_out, in_3);
  and and_12 (and_12_out, not_2_out, not_3_out, not_4_out);
  and and_13 (and_13_out, not_1_out, not_2_out, in_2);
  and and_14 (and_14_out, not_1_out, in_2, not_4_out);
  and and_15 (and_15_out, not_1_out, in_3, not_3_out, min);
  and and_16 (and_16_out, not_2_out, not_3_out, not_4_out);
  and and_17 (and_17_out, not_1_out, in_2, not_4_out);
  and and_18 (and_18_out, not_1_out, not_3_out, not_4_out);
  and and_19 (and_19_out, not_1_out, in_3, not_3_out);
  and and_20 (and_20_out, not_1_out, in_3, not_4_out);
  and and_21 (and_21_out, max, not_2_out, not_3_out);
  and and_22 (and_22_out, not_1_out, not_2_out, in_2);
  and and_23 (and_23_out, not_1_out, in_3, not_3_out);
  and and_24 (and_24_out, not_1_out, in_3, not_4_out);
  and and_25 (and_25_out, max, not_2_out, not_3_out);
  or or_1 (a, and_1_out, and_2_out, and_3_out, and_4_out);
  or or_2 (b, and_5_out, and_6_out, and_7_out, and_8_out);
  or or_3 (c, and_9_out, and_10_out, and_11_out);
  or or_4 (d, and_12_out, and_13_out, and_14_out, and_15_out);
  or or_5 (e, and_16_out, and_17_out);
  or or_6 (f, and_18_out, and_19_out, and_20_out, and_21_out);
  or or_7 (g, and_22_out, and_23_out, and_24_out, and_25_out);
endmodule

module BCD7SEGx2 (
  input  [6:0] inBCDx2,
  output Dg,
  output Df,
  output De,
  output Dd,
  output Dc,
  output Db,
  output Da,
  output Ug,
  output Uf,
  output Ue,
  output Ud,
  output Uc,
  output Ub,
  output Ua
);

  wire [6:0] divider_1_out, divider_1_rem;

  Divider #(.width(7)) divider_1 (
    .a(inBCDx2), .b(7'b0001010), .out(divider_1_out), .rem(divider_1_rem));  // open: upper
  // Probe on divider_1_rem
  // Probe on divider_1_out
  _7_Segment_Display u_7_segment_display_1 (.g(Dg), .f(Df), .a(Da), .b(Db), .e(De), .d(Dd), .c(Dc));  // open: dp
  _7_Segment_Display u_7_segment_display_2 (.g(Ug), .f(Uf), .a(Ua), .b(Ub), .e(Ue), .d(Ud), .c(Uc));  // open: dp
  BCD7SEG Decenas (
    .min(divider_1_out[0]), .in_2(divider_1_out[1]), .in_3(divider_1_out[2]), .max(divider_1_out[3]), .a(Da),
    .b(Db), .c(Dc), .d(Dd), .e(De), .f(Df), .g(Dg));
  BCD7SEG Unidades (
    .min(divider_1_rem[0]), .in_2(divider_1_rem[1]), .in_3(divider_1_rem[2]), .max(divider_1_rem[3]), .a(Ua),
    .b(Ub), .c(Uc), .d(Ud), .e(Ue), .f(Uf), .g(Ug));

  // Other names for the same wires on the sheet: a = Da; a1 = Ua; b = Db; b1 = Ub; c = Dc; c1 = Uc; d = Dd; d1 = Ud;
  //   e = De; e1 = Ue; f = Df; f1 = Uf; g = Dg; g1 = Ug
endmodule

module ContadorUnitario (
  input  action,
  input  push,
  input  Reset,
  output [6:0] Decenas,
  output [6:0] Unidades
);

  wire and_1_out, j_k_ff_1_qn, j_k_ff_2_qn, j_k_ff_3_qn, j_k_ff_4_qn, j_k_ff_5_qn, j_k_ff_6_qn, or_1_out;
  wire [6:0] j_k_ff_1_q;

  or or_1 (or_1_out, Reset, and_1_out);
  J_K_Flip_Flop j_k_ff_1 (
    .J(action), .K(action), .clk(push), .Q(j_k_ff_1_q[0]), .Qn(j_k_ff_1_qn), .reset(or_1_out));  // open: preset
  and and_1 (and_1_out, j_k_ff_1_q[6], j_k_ff_1_q[5], j_k_ff_1_q[2]);
  J_K_Flip_Flop j_k_ff_2 (
    .J(action), .K(action), .clk(j_k_ff_1_qn), .Q(j_k_ff_1_q[1]), .Qn(j_k_ff_2_qn), .reset(or_1_out));  // open: preset
  BCD7SEGx2 bcd7segx2_1 (
    .inBCDx2(j_k_ff_1_q), .Dg(Decenas[6]), .Df(Decenas[5]), .De(Decenas[4]), .Dd(Decenas[3]),
    .Dc(Decenas[2]), .Db(Decenas[1]), .Da(Decenas[0]), .Ug(Unidades[6]), .Uf(Unidades[5]), .Ue(Unidades[4]),
    .Ud(Unidades[3]), .Uc(Unidades[2]), .Ub(Unidades[1]), .Ua(Unidades[0]));
  J_K_Flip_Flop j_k_ff_3 (
    .J(action), .K(action), .clk(j_k_ff_2_qn), .Q(j_k_ff_1_q[2]), .Qn(j_k_ff_3_qn), .reset(or_1_out));  // open: preset
  J_K_Flip_Flop j_k_ff_4 (
    .J(action), .K(action), .clk(j_k_ff_3_qn), .Q(j_k_ff_1_q[3]), .Qn(j_k_ff_4_qn), .reset(or_1_out));  // open: preset
  J_K_Flip_Flop j_k_ff_5 (
    .J(action), .K(action), .clk(j_k_ff_4_qn), .Q(j_k_ff_1_q[4]), .Qn(j_k_ff_5_qn), .reset(or_1_out));  // open: preset
  J_K_Flip_Flop j_k_ff_6 (
    .J(action), .K(action), .clk(j_k_ff_5_qn), .Q(j_k_ff_1_q[5]), .Qn(j_k_ff_6_qn), .reset(or_1_out));  // open: preset
  J_K_Flip_Flop j_k_ff_7 (
    .J(action), .K(action), .clk(j_k_ff_6_qn), .Q(j_k_ff_1_q[6]), .reset(or_1_out));  // open: Qn, preset
  _7_Segment_Display u_7_segment_display_1 (
    .g(Decenas[6]), .f(Decenas[5]), .a(Decenas[0]), .b(Decenas[1]), .e(Decenas[4]), .d(Decenas[3]),
    .c(Decenas[2]));  // open: dp
  _7_Segment_Display u_7_segment_display_2 (
    .g(Unidades[6]), .f(Unidades[5]), .a(Unidades[0]), .b(Unidades[1]), .e(Unidades[4]), .d(Unidades[3]),
    .c(Unidades[2]));  // open: dp

  // Other names for the same wires on the sheet: a = Decenas[0]; b = Decenas[1]; c = Decenas[2]; d = Decenas[3];
  //   e = Decenas[4]; f = Decenas[5]; g = Decenas[6]; a1 = Unidades[0]; b1 = Unidades[1]; c1 = Unidades[2];
  //   d1 = Unidades[3]; e1 = Unidades[4]; f1 = Unidades[5]; g1 = Unidades[6]
endmodule
